# Fritzing sketch Schematic (saved by Fritzing 0.9.3b)
breadboards: 1

parts:
  A1 = MAX6675 module [package=THT]
  A2 = MAX6675 module [package=THT]
  A3 = MAX6675 module [package=THT]
  A4 = MAX6675 module [package=THT]
  A5 = MAX6675 module [package=THT]
  A6 = MAX6675 module [package=THT]
  SW-1 = Vibration sensor module
  SW-2 = Vibration sensor module
  SW-3 = Vibration sensor module
  SW-4 = Vibration sensor module
  Part1 = Arduino Mega 2560 (Rev3)

nets:
  N1: A1.pin1, A2.pin1, A3.pin1, A4.pin1, A5.pin1, A6.pin1, SW-1.Ground, SW-2.Ground, SW-3.Ground, SW-4.Ground, Part1.GND
  VCC: A1.pin2, A2.pin2, A3.pin2, A4.pin2, A5.pin2, A6.pin2, SW-1.vcc, SW-2.vcc, SW-3.vcc, SW-4.vcc, Part1.5V
  N2: A1.pin3, Part1.D42
  N3: A1.pin4, Part1.D26
  N4: A1.pin5, Part1.D40
  N5: A2.pin3, Part1.D46
  N6: A2.pin4, Part1.D25
  N7: A2.pin5, Part1.D44
  N8: A3.pin3, Part1.D34
  N9: A3.pin4, Part1.D24
  N10: A3.pin5, Part1.D32
  N11: A4.pin3, Part1.D47
  N12: A4.pin4, Part1.D27
  N13: A4.pin5, Part1.D48
  N14: A5.pin3, Part1.D10_PWM
  N15: A5.pin4, Part1.D28
  N16: A5.pin5, Part1.D11_PWM
  N17: A6.pin3, Part1.D8_PWM
  N18: A6.pin4, Part1.D22
  N19: A6.pin5, Part1.D9_PWM
  N20: SW-1.Digital_output, Part1.D2_PWM
  N21: SW-2.Digital_output, Part1.D4_PWM
  N22: SW-3.Digital_output, Part1.D3_PWM
  N23: SW-4.Digital_output, Part1.D5_PWM

custom parts:
  MAX6675 module: MAX6675 Module + K Type Thermocouple Sensor Temperature Degrees.
  Vibration sensor module: Single-roller type full induction trigger switch. When no vibration or tilt, the product is ON conduction state, and in the steady state, when a vibration or tilt, the switch will be rendered instantly disconnect the conductive resistance increases, generating a current pulse signal, thereby triggering circuit. The default state of the swith is close Digital output Supply voltage:3.3V-5V On-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
